// Logisim project Single Cycle Processor.circ as structural Verilog
module ALU (
  input  [1:0] Shift_Op,
  input  [31:0] A,
  input  Arithmetic_Op,
  input  [31:0] B,
  input  [1:0] Logical_Op,
  input  [1:0] ALU_Selection,
  output [31:0] ALU_result,
  output overflow,
  output [31:0] zero
);

  wire [31:0] adder_1_out, and_1_out, multiplexer_1_out, not_1_out, or_1_out, Shifter_data_out, xor_1_out,
       xor_2_out;
  wire [31:1] undriven;

  assign xor_1_out = B ^ {undriven, Arithmetic_Op};  // XOR_Gate xor_1, 32 bits wide
  assign and_1_out = A & B;  // AND_Gate and_1, 32 bits wide
  assign not_1_out = ~or_1_out;  // NOT_Gate not_1, 32 bits wide
  assign or_1_out = A | B;  // OR_Gate or_1, 32 bits wide
  assign xor_2_out = A ^ B;  // XOR_Gate xor_2, 32 bits wide
  Shifter Shifter (.Data(B), .Shift_amount(A[4:0]), .Shift_Op(Shift_Op), .Data_out(Shifter_data_out));
  Adder #(.width(32)) adder_1 (.a(A), .b(xor_1_out), .out(adder_1_out), .cin(Arithmetic_Op), .cout(overflow));
  Multiplexer #(.select(2), .width(32), .enable("false")) multiplexer_1 (
    .in0(and_1_out), .in1(or_1_out), .in2(not_1_out), .in3(xor_2_out), .out(multiplexer_1_out),
    .sel(Logical_Op));
  Multiplexer #(.select(2), .width(32), .enable("false")) multiplexer_2 (
    .in0(Shifter_data_out), .in2(adder_1_out), .in3(multiplexer_1_out), .out(ALU_result), .sel(ALU_Selection));  // open: in1
  assign zero = ~ALU_result;  // NOT_Gate not_2, 32 bits wide
  // Pins of 1 and 32 bits meet at {undriven, Arithmetic_Op}
endmodule

module Shifter (
  input  [31:0] Data,
  input  [4:0] Shift_amount,
  input  [1:0] Shift_Op,
  output [31:0] Data_out
);

  wire [31:0] shifter_1_out, shifter_2_out, shifter_3_out, shifter_4_out;

  Shifter_part #(.width(32)) shifter_1 (.in(Data), .\dist (Shift_amount), .out(shifter_1_out));
  Shifter_part #(.width(32), .shift("lr")) shifter_2 (.in(Data), .\dist (Shift_amount), .out(shifter_2_out));
  Shifter_part #(.width(32), .shift("ar")) shifter_3 (.in(Data), .\dist (Shift_amount), .out(shifter_3_out));
  Shifter_part #(.width(32), .shift("rr")) shifter_4 (.in(Data), .\dist (Shift_amount), .out(shifter_4_out));
  Multiplexer #(.select(2), .width(32), .enable("false")) multiplexer_1 (
    .in0(shifter_1_out), .in1(shifter_2_out), .in2(shifter_3_out), .in3(shifter_4_out), .out(Data_out),
    .sel(Shift_Op));
endmodule
